# Fritzing sketch Simon Dice (saved by Fritzing 0.9.3b)
circuit board: 5.9cm x 5.39959cm
breadboards: 1

parts:
  ProfeDice = Arduino Uno (Rev3)
  SW-VE = Momentary Switch [package=ksa_sealed_tac_switch]
  SW-AM = Momentary Switch [package=ksa_sealed_tac_switch]
  SW-AZ = Momentary Switch [package=ksa_sealed_tac_switch]
  SW-RO = Momentary Switch [package=ksa_sealed_tac_switch]
  Buzzer = Buzzer 12mm [package=buzzer-12mm-ns-kit]
  VERDE = LED - 5mm [color="Red (633nm)" package="5 mm [THT]"]
  AMARILLO = LED - 5mm [color="Red (633nm)" package="5 mm [THT]"]
  AZUL = LED - 5mm [color="Red (633nm)" package="5 mm [THT]"]
  ROJO = LED - 5mm [color="Red (633nm)" package="5 mm [THT]"]
  R1 = Resistor [tolerance=±5% resistance=1k package=THT]
  R2 = Resistor [tolerance=±5% resistance=1k package=THT]
  R3 = Resistor [tolerance=±5% resistance=1k package=THT]
  R4 = Resistor [tolerance=±5% resistance=1k package=THT]
  R5 = Resistor [tolerance=±5% resistance=10k package=THT]
  R6 = Resistor [tolerance=±5% resistance=10k package=THT]
  R7 = Resistor [tolerance=±5% resistance=10k package=THT]
  R8 = Resistor [tolerance=±5% resistance=10k package=THT]

nets:
  N1: ProfeDice.A0, SW-RO.3, R7.Pin_0
  N2: ProfeDice.A1, SW-VE.4, R5.Pin_1
  N3: ProfeDice.A2, SW-AM.4, R6.Pin_1
  N4: ProfeDice.A3, SW-AZ.3, R8.Pin_0
  N5: ProfeDice.D2, R4.Pin_1
  N6: ProfeDice.D3_PWM, R1.Pin_0
  N7: ProfeDice.D4, R2.Pin_0
  N8: ProfeDice.D5_PWM, R3.Pin_1
  N9: ProfeDice.D7, Buzzer.1
  N10: ProfeDice.5V, R5.Pin_0, R6.Pin_0, R7.Pin_1, R8.Pin_1
  N11: ProfeDice.GND, SW-VE.2, SW-AM.2, SW-AZ.1, SW-RO.1, Buzzer.2, VERDE.cathode, AMARILLO.cathode, AZUL.cathode, ROJO.cathode
  N12: VERDE.anode, R1.Pin_1
  N13: AMARILLO.anode, R2.Pin_1
  N14: AZUL.anode, R3.Pin_0
  N15: ROJO.anode, R4.Pin_0
