# Fritzing sketch 4 channel relay module (saved by Fritzing 0.9.3b)

parts:
  Part1 = Arduino Uno (Rev3)
  U1 = 4-Channel 5v Relay Shield [package=relay-4ch5v10a]
  LED1 = LED - 5mm [color="Red (633nm)" package="5 mm [THT]"]
  J1 = Screw terminal - 2 pins [package=THT]

nets:
  GND: Part1.GND, U1.GND
  N1: Part1.D4, U1.IN1
  N2: Part1.D5_PWM, U1.IN2
  N3: Part1.D6_PWM, U1.IN3
  N4: Part1.D7, U1.IN4
  5V: Part1.5V, U1.VCC
  N5: U1.K4-Off, J1.pin1
  N6: U1.K4-On, LED1.anode
  N7: LED1.cathode, J1.pin2

custom parts:
  4-Channel 5v Relay Shield: 4 Channel 5v Relay Shield w. 2x SPD-06VDC-SD-C
