# Fritzing sketch Digispark and RGB LED (saved by Fritzing 0.9.2b)
breadboards: 1

parts:
  Digispark1 = Digispark
  R1 = Resistor [tolerance=±5% resistance=1k package=THT]
  LED2 = RGB LED - (4 legs) [package="5 mm [THT]"]
  R2 = Resistor [tolerance=±5% resistance=1k package=THT]
  R3 = Resistor [tolerance=±5% resistance=1k package=THT]

nets:
  N1: Digispark1.VCC, LED2.common_anode
  N2: Digispark1.P1, R1.Pin_0
  N3: Digispark1.P2, R2.Pin_0
  N4: Digispark1.P3, R3.Pin_0
  N5: R1.Pin_1, LED2.red_cathode
  N6: LED2.green_cathode, R2.Pin_1
  N7: LED2.blue_cathode, R3.Pin_1

custom parts:
  Digispark: The Digispark is an Attiny85 based microcontroller development board similar to the Arduino line, only cheaper, smaller, and a bit less powerful. With a whole host of shields to extend its functionality and the ability to use the familiar Arduino IDE the Digispark is a great way to jump into electronics, or perfect for when an Arduino is too big or too much.
