# Fritzing sketch arduino and ADXL245 (saved by Fritzing 0.9.3b)

parts:
  Part6 = Arduino Uno (Rev3)
  Part8 = Adafruit ADXL345 [part_number="Adafruit #1231"]

nets:
  N1: Part6.A4/SDA, Part8.SDA/SDIO
  N2: Part6.A5/SCL, Part8.SCL
  5V: Part6.5V, Part8.VIN
  GND: Part6.GND, Part8.GND

custom parts:
  Adafruit ADXL345: Filling out our accelerometer offerings, we now have the really lovely digital ADXL345 from Analog Devices, a triple-axis accelerometer with digital I2C and SPI interface breakout. We added an on-board 3.3V regulator and logic-level shifting circuitry, making it a perfect choice for interfacing with any 3V or 5V microcontroller such as the Arduino. The sensor has three axes of measurements, X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
